# Fritzing sketch RobotMecanum (saved by Fritzing 1.0.7)
circuit board: 8.46667cm x 5.64444cm
breadboards: 1

parts:
  Mod1 = Amica NodeMCU DEVKIT 1.0
  U1 = 74HC595 [package="DIP16 [THT]"]
  Componente1 = Motor Driver 1A Dual TB6612FNG
  BATT1 = LiPoly Battery (1300mAh)
  M1 = gear-motor
  M2 = gear-motor

nets:
  GND: Mod1.pin1, Mod1.pin2, Mod1.pin_9, Mod1.pin_10, Mod1.pin_25, Mod1.pin_26, Mod1.pin_29, U1.GND, U1.OE, Componente1.GND, BATT1.negative
  N1: Mod1.pin6, Componente1.PWMB
  N2: Mod1.pin7, Componente1.PWMA
  N3: Mod1.pin_11, U1.SH_CP
  N4: Mod1.pin_12, U1.DS
  N5: Mod1.pin_15, Componente1.STBY
  N6: Mod1.pin_19, U1.ST_CP
  N7: U1.Q1, Componente1.AIN1
  N8: U1.Q2, Componente1.BIN2
  N9: U1.Q3, Componente1.BIN1
  VCC: U1.MR, U1.VCC, Componente1.VCC
  N10: U1.Q0, Componente1.AIN2
  N11: Componente1.B01, M2.pin_1
  N12: Componente1.B02, M2.pin_2
  N13: Componente1.A02, M1.pin_1
  N14: Componente1.A01, M1.pin_2
  N15: Componente1.VM, BATT1.positive
